# Fritzing sketch Smoke Detector (saved by Fritzing 0.9.3b)
circuit board: 8.46667cm x 5.64444cm
breadboards: 1

parts:
  U1 = GAS_SENSOR [package=mq-3]
  U2 = NodeMCU V1.0

nets:
  N1: U1.B1, U2.GND
  N2: U1.H1, U2.3V3

custom parts:
  NodeMCU V1.0: ESP8266 based NodeMCU

// code stored in the sketch: Smoke Detector.ino
#include <Blynk.h>


//Blynk MQ-2 Smoke Detector
#include <ESP8266WiFi.h>
#include <BlynkSimpleEsp8266.h>
//#include <SimpleTimer.h>
//#define BLYNK_PRINT Serial    // Comment this out to disable prints and save space
char auth[] = "vt9SFMRsZ9uEgSjg3MqdF3cwOe8Kosu7"; //Enter Authentication code sent by Blynk
 

char ssid[] = "GEARBOX STAFF"; //Enter WIFI Name
char pass[] = "Staff@Gearbox"; //Enter WIFI Password
 
SimpleTimer timer;
 
int mq2 = A0; // smoke sensor is connected with the analog pin A0 
int data = 0; 
void setup() 
{
  Serial.begin(115200);
  Blynk.begin(auth, ssid, pass);
  timer.setInterval(1000L, getSendData);
}
 
void loop() 
{
  timer.run(); // Initiates SimpleTimer
  Blynk.run();
}
 
void getSendData()
{
data = analogRead(mq2); 
  Blynk.virtualWrite(V2, data);
 
  if (data > 700 )
  {
    Blynk.notify("Smoke Detected!"); 
  }
 
}
